// Logisim project myAlu.circ as structural Verilog
module myNOT (
  input  in_1,
  output out_2
);

  nand nand_1 (out_2, in_1, in_1);
endmodule

module myAND (
  input  in_1,
  input  in_2,
  output out_3
);

  wire nand_1_out;

  nand nand_1 (nand_1_out, in_1, in_2);
  myNOT mynot_1 (.in_1(nand_1_out), .out_2(out_3));
endmodule

module myOR (
  input  in_1,
  input  in_2,
  output out_3
);

  wire mynot_1_out_2, mynot_2_out_2;

  myNOT mynot_1 (.in_1(in_1), .out_2(mynot_1_out_2));
  myNOT mynot_2 (.in_1(in_2), .out_2(mynot_2_out_2));
  nand nand_1 (out_3, mynot_1_out_2, mynot_2_out_2);
endmodule

module myXOR (
  input  in_1,
  input  in_2,
  output out_3
);

  wire myand_1_out_3, myand_2_out_3, mynot_1_out_2, mynot_2_out_2;

  myNOT mynot_1 (.in_1(in_1), .out_2(mynot_1_out_2));
  myNOT mynot_2 (.in_1(in_2), .out_2(mynot_2_out_2));
  myAND myand_1 (.in_1(mynot_1_out_2), .in_2(in_2), .out_3(myand_1_out_3));
  myAND myand_2 (.in_1(in_1), .in_2(mynot_2_out_2), .out_3(myand_2_out_3));
  myOR myor_1 (.in_1(myand_1_out_3), .in_2(myand_2_out_3), .out_3(out_3));
endmodule

module myMUX (
  input  in_1,
  input  in_2,
  input  in_3,
  output out_4
);

  wire myand_1_out_3, myand_2_out_3, mynot_1_out_2;

  myNOT mynot_1 (.in_1(in_3), .out_2(mynot_1_out_2));
  myAND myand_1 (.in_1(in_1), .in_2(mynot_1_out_2), .out_3(myand_1_out_3));
  myAND myand_2 (.in_1(in_2), .in_2(in_3), .out_3(myand_2_out_3));
  myXOR myxor_1 (.in_1(myand_1_out_3), .in_2(myand_2_out_3), .out_3(out_4));
endmodule

module myDMUX (
  input  in_1,
  input  in_2,
  output out_3,
  output out_4
);

  wire mynot_1_out_2;

  myNOT mynot_1 (.in_1(in_2), .out_2(mynot_1_out_2));
  myAND myand_1 (.in_1(in_1), .in_2(mynot_1_out_2), .out_3(out_3));
  myAND myand_2 (.in_1(in_1), .in_2(in_2), .out_3(out_4));
endmodule

module myHalfAdder (
  input  in_1,
  input  in_2,
  output S,
  output C
);

  myXOR myxor_1 (.in_1(in_1), .in_2(in_2), .out_3(S));
  myAND myand_1 (.in_1(in_1), .in_2(in_2), .out_3(C));
endmodule

module myFullAdder (
  input  in_1,
  input  in_2,
  input  in_3,
  output S,
  output C
);

  wire myhalfadder_1_c, myhalfadder_1_s, myhalfadder_2_c;

  myHalfAdder myhalfadder_1 (.in_1(in_2), .in_2(in_3), .S(myhalfadder_1_s), .C(myhalfadder_1_c));
  myHalfAdder myhalfadder_2 (.in_1(in_1), .in_2(myhalfadder_1_s), .S(S), .C(myhalfadder_2_c));
  myOR myor_1 (.in_1(myhalfadder_2_c), .in_2(myhalfadder_1_c), .out_3(C));
endmodule
